// Logisim project RiscV.circ as structural Verilog: 4 circuits, main circuit main
module main (
  input  RegWrite,
  input  ALUScr
);

  wire button_1_out, clock_1_out, clock_2_out;
  wire [31:0] adder_1_out, bancoregistradores_1_rs1, bancoregistradores_1_rs2, bit_extender_1_out,
       multiplexer_1_out, register_1_q, rom_1_data, ula_1_datad;

  Clock clock_1 (.out(clock_1_out));
  Register #(.width(32)) register_1 (
    .D(adder_1_out), .en(clock_1_out), .clk(clock_1_out), .Q(register_1_q), .clr(button_1_out));
  Button button_1 (.out(button_1_out));
  Adder #(.width(32)) adder_1 (.a(register_1_q), .b(32'h4), .out(adder_1_out));  // open: cin, cout
  ROM #(.addrWidth(24), .dataWidth(32)) rom_1 (.addr(register_1_q[23:0]), .data(rom_1_data));
  // Probe on rom_1_data[19:15]
  // Probe on rom_1_data[11:7]
  // Probe on rom_1_data[24:20]
  Clock clock_2 (.out(clock_2_out));
  ImediatoGenerator imediatogenerator_1 ();  // open: Instruction_SET
  // Probe on ula_1_datad
  bancoRegistradores bancoregistradores_1 (
    .clk(clock_2_out), .rsi2(rom_1_data[24:20]), .rdi(rom_1_data[11:7]), .data(ula_1_datad), .WE(RegWrite),
    .rsi1(rom_1_data[19:15]), .rs1(bancoregistradores_1_rs1), .rs2(bancoregistradores_1_rs2));
  Bit_Extender #(.in_width(12), .out_width(32), .\type ("zero")) bit_extender_1 (.out(bit_extender_1_out));  // open: in
  Multiplexer #(.width(32)) multiplexer_1 (
    .in0(bancoregistradores_1_rs2), .in1(bit_extender_1_out), .out(multiplexer_1_out), .sel(ALUScr));
  // Probe on bancoregistradores_1_rs1
  // Probe on multiplexer_1_out
  ULA ula_1 (
    .sel(4'b0010), .dataA(bancoregistradores_1_rs1), .dataB(multiplexer_1_out), .dataD(ula_1_datad));  // open: zero
  RAM #(.addrWidth(12), .dataWidth(32)) ram_1 ();  // open: addr, we, oe, clk, din, dout

  // Notes on the sheet:
  //   contents of rom_1 (hex, n*v repeats v):
  //   500093 0 0 0 300113 0 0 0 2080b3
endmodule

module bancoRegistradores (
  input  [4:0] rsi1,
  input  [4:0] rsi2,
  input  [4:0] rdi,
  input  [31:0] data,
  input  WE,
  input  clk,
  output [31:0] rs1,
  output [31:0] rs2
);

  wire x0we_t, x1we_t, x2we_t, x3we_t, x4we_t, x5we_t, x6we_t, x7we_t, x8we_t, x9we_t, x10we_t, x11we_t,
       x12we_t, x13we_t, x14we_t, x15we_t, x16we_t, x17we_t, x18we_t, x19we_t, x20we_t, x21we_t, x22we_t,
       x23we_t, x24we_t, x25we_t, x26we_t, x27we_t, x28we_t, x29we_t, x30we_t, x31we_t;
  wire [31:0] x1q_t, x2q_t, x3q_t, x4q_t, x5q_t, x6q_t, x7q_t, x8q_t, x9q_t, x10q_t, x11q_t, x12q_t, x13q_t,
       x14q_t, x15q_t, x16q_t, x17q_t, x18q_t, x19q_t, x20q_t, x21q_t, x22q_t, x23q_t, x24q_t, x25q_t,
       x26q_t, x27q_t, x28q_t, x29q_t, x30q_t, x31q_t;

  Demultiplexer #(.select(5)) demultiplexer_1 (
    .out0(x0we_t), .out1(x1we_t), .out2(x2we_t), .out3(x3we_t), .out4(x4we_t), .out5(x5we_t), .out6(x6we_t),
    .out7(x7we_t), .out8(x8we_t), .out9(x9we_t), .out10(x10we_t), .out11(x11we_t), .out12(x12we_t),
    .out13(x13we_t), .out14(x14we_t), .out15(x15we_t), .out16(x16we_t), .out17(x17we_t), .out18(x18we_t),
    .out19(x19we_t), .out20(x20we_t), .out21(x21we_t), .out22(x22we_t), .out23(x23we_t), .out24(x24we_t),
    .out25(x25we_t), .out26(x26we_t), .out27(x27we_t), .out28(x28we_t), .out29(x29we_t), .out30(x30we_t),
    .out31(x31we_t), .in(WE), .sel(rdi));
  Register #(.width(32)) x4 (.D(data), .en(x4we_t), .clk(clk), .Q(x4q_t));  // open: clr
  Register #(.width(32)) x8 (.D(data), .en(x8we_t), .clk(clk), .Q(x8q_t));  // open: clr
  Register #(.width(32)) x12 (.D(data), .en(x12we_t), .clk(clk), .Q(x12q_t));  // open: clr
  Register #(.width(32)) x16 (.D(data), .en(x16we_t), .clk(clk), .Q(x16q_t));  // open: clr
  Register #(.width(32)) x20 (.D(data), .en(x20we_t), .clk(clk), .Q(x20q_t));  // open: clr
  Register #(.width(32)) x24 (.D(data), .en(x24we_t), .clk(clk), .Q(x24q_t));  // open: clr
  Register #(.width(32)) x28 (.D(data), .en(x28we_t), .clk(clk), .Q(x28q_t));  // open: clr
  Register #(.width(32)) x1 (.D(data), .en(x1we_t), .clk(clk), .Q(x1q_t));  // open: clr
  Register #(.width(32)) x5 (.D(data), .en(x5we_t), .clk(clk), .Q(x5q_t));  // open: clr
  Register #(.width(32)) x9 (.D(data), .en(x9we_t), .clk(clk), .Q(x9q_t));  // open: clr
  Register #(.width(32)) x13 (.D(data), .en(x13we_t), .clk(clk), .Q(x13q_t));  // open: clr
  Register #(.width(32)) x17 (.D(data), .en(x17we_t), .clk(clk), .Q(x17q_t));  // open: clr
  Register #(.width(32)) x21 (.D(data), .en(x21we_t), .clk(clk), .Q(x21q_t));  // open: clr
  Register #(.width(32)) x25 (.D(data), .en(x25we_t), .clk(clk), .Q(x25q_t));  // open: clr
  Register #(.width(32)) x29 (.D(data), .en(x29we_t), .clk(clk), .Q(x29q_t));  // open: clr
  Register #(.width(32)) x2 (.D(data), .en(x2we_t), .clk(clk), .Q(x2q_t));  // open: clr
  Register #(.width(32)) x6 (.D(data), .en(x6we_t), .clk(clk), .Q(x6q_t));  // open: clr
  Register #(.width(32)) x10 (.D(data), .en(x10we_t), .clk(clk), .Q(x10q_t));  // open: clr
  Register #(.width(32)) x14 (.D(data), .en(x14we_t), .clk(clk), .Q(x14q_t));  // open: clr
  Register #(.width(32)) x18 (.D(data), .en(x18we_t), .clk(clk), .Q(x18q_t));  // open: clr
  Register #(.width(32)) x22 (.D(data), .en(x22we_t), .clk(clk), .Q(x22q_t));  // open: clr
  Register #(.width(32)) x26 (.D(data), .en(x26we_t), .clk(clk), .Q(x26q_t));  // open: clr
  Register #(.width(32)) x30 (.D(data), .en(x30we_t), .clk(clk), .Q(x30q_t));  // open: clr
  Register #(.width(32)) x3 (.D(data), .en(x3we_t), .clk(clk), .Q(x3q_t));  // open: clr
  Register #(.width(32)) x7 (.D(data), .en(x7we_t), .clk(clk), .Q(x7q_t));  // open: clr
  Register #(.width(32)) x11 (.D(data), .en(x11we_t), .clk(clk), .Q(x11q_t));  // open: clr
  Register #(.width(32)) x15 (.D(data), .en(x15we_t), .clk(clk), .Q(x15q_t));  // open: clr
  Register #(.width(32)) x19 (.D(data), .en(x19we_t), .clk(clk), .Q(x19q_t));  // open: clr
  Register #(.width(32)) x23 (.D(data), .en(x23we_t), .clk(clk), .Q(x23q_t));  // open: clr
  Register #(.width(32)) x27 (.D(data), .en(x27we_t), .clk(clk), .Q(x27q_t));  // open: clr
  Register #(.width(32)) x31 (.D(data), .en(x31we_t), .clk(clk), .Q(x31q_t));  // open: clr
  Multiplexer #(.select(5), .width(32)) multiplexer_1 (
    .in0({32{1'b0}}), .in1(x1q_t), .in2(x2q_t), .in3(x3q_t), .in4(x4q_t), .in5(x5q_t), .in6(x6q_t),
    .in7(x7q_t), .in8(x8q_t), .in9(x9q_t), .in10(x10q_t), .in11(x11q_t), .in12(x12q_t), .in13(x13q_t),
    .in14(x14q_t), .in15(x15q_t), .in16(x16q_t), .in17(x17q_t), .in18(x18q_t), .in19(x19q_t), .in20(x20q_t),
    .in21(x21q_t), .in22(x22q_t), .in23(x23q_t), .in24(x24q_t), .in25(x25q_t), .in26(x26q_t), .in27(x27q_t),
    .in28(x28q_t), .in29(x29q_t), .in30(x30q_t), .in31(x31q_t), .out(rs1), .sel(rsi1));
  Multiplexer #(.select(5), .width(32)) multiplexer_2 (
    .in0({32{1'b0}}), .in1(x1q_t), .in2(x2q_t), .in3(x3q_t), .in4(x4q_t), .in5(x5q_t), .in6(x6q_t),
    .in7(x7q_t), .in8(x8q_t), .in9(x9q_t), .in10(x10q_t), .in11(x11q_t), .in12(x12q_t), .in13(x13q_t),
    .in14(x14q_t), .in15(x15q_t), .in16(x16q_t), .in17(x17q_t), .in18(x18q_t), .in19(x19q_t), .in20(x20q_t),
    .in21(x21q_t), .in22(x22q_t), .in23(x23q_t), .in24(x24q_t), .in25(x25q_t), .in26(x26q_t), .in27(x27q_t),
    .in28(x28q_t), .in29(x29q_t), .in30(x30q_t), .in31(x31q_t), .out(rs2), .sel(rsi2));

  // Other names for the same wires on the sheet: clk_t = clk; rd_t[31:0] = data; rdi_t[4:0] = rdi; rs1_t[31:0] = rs1;
  //   rs2_t[31:0] = rs2; rsi1_t[4:0] = rsi1; rsi2_t[4:0] = rsi2; we_t = WE
endmodule

module ULA (
  input  [31:0] dataA,
  input  [31:0] dataB,
  input  [3:0] sel,
  output [31:0] dataD,
  output zero
);

  wire [31:0] adder_1_out, and_1_out, or_1_out, subtractor_1_out;

  assign and_1_out = dataA & dataB;  // AND_Gate and_1, 32 bits wide
  assign or_1_out = dataA | dataB;  // OR_Gate or_1, 32 bits wide
  Adder #(.width(32)) adder_1 (.a(dataA), .b(dataB), .out(adder_1_out));  // open: cin, cout
  Subtractor #(.width(32)) subtractor_1 (.a(dataA), .b(dataB), .out(subtractor_1_out));  // open: bin, bout
  Multiplexer #(.select(4), .width(32)) multiplexer_1 (
    .in0(and_1_out), .in1(or_1_out), .in2(adder_1_out), .in3(dataA), .in4(dataA), .in5(dataA),
    .in6(subtractor_1_out), .in7(dataA), .in8(dataA), .in9(dataA), .in10(dataA), .in11(dataA), .in12(dataA),
    .in13(dataA), .in14(dataA), .in15(dataA), .out(dataD), .sel(sel));
  nor nor_1 (zero, dataD[0], dataD[1], dataD[2], dataD[3], dataD[4], dataD[5], dataD[6], dataD[7], dataD[8], dataD[9], dataD[10], dataD[11], dataD[12], dataD[13], dataD[14], dataD[15], dataD[16], dataD[17], dataD[18], dataD[19], dataD[20], dataD[21], dataD[22], dataD[23], dataD[24], dataD[25], dataD[26], dataD[27], dataD[28], dataD[29], dataD[30], dataD[31]);

  // Other names for the same wires on the sheet: dataA_t[31:0] = dataA; dataB_t[31:0] = dataB; dataD_t[31:0] = dataD;
  //   sel_t[3:0] = sel

  // Notes on the sheet:
  //   0000 and
  //   0001 or
  //   0010 add
  //   0110 sub
  //   21
  //   depois implementos o restante
endmodule

module ImediatoGenerator (
  input  [31:0] Instruction_SET
);

  wire [31:20] undriven;

  // Probe on undriven

  // Notes on the sheet:
  //   s type
  //   tipo i
  //   type B
endmodule
