// Digital circuit Banco de Registradores.dig as structural Verilog
module Banco_de_Registradores (
  input  rd_0,
  input  rd_1,
  input  rd_2,
  input  rd_3,
  input  rd_4,
  input  rd_5,
  input  rd_6,
  input  rd_7,
  input  enable,
  input  clk
);

  wire demux_1_b1, demux_1_b2, demux_1_b3, demux_1_b4, demux_1_b5, demux_1_b6, demux_1_b7;

  Demux demux_1 (
    .Enable(enable), .B1(demux_1_b1), .B2(demux_1_b2), .B3(demux_1_b3), .B4(demux_1_b4), .B5(demux_1_b5),
    .B6(demux_1_b6), .B7(demux_1_b7));  // open: S2, S1, S0, B0
  Registrador Reg1 (
    .in_0(rd_0), .in_1(rd_1), .in_2(rd_2), .in_3(rd_3), .in_4(rd_4), .in_5(rd_5), .in_6(rd_6), .in_7(rd_7),
    .clk(clk), .Enable(demux_1_b1));  // open: out_0, out_1, out_2, out_3, out_4, out_5, out_6, out_7
  Registrador Reg2 (
    .in_0(rd_0), .in_1(rd_1), .in_2(rd_2), .in_3(rd_3), .in_4(rd_4), .in_5(rd_5), .in_6(rd_6), .in_7(rd_7),
    .clk(clk), .Enable(demux_1_b2));  // open: out_0, out_1, out_2, out_3, out_4, out_5, out_6, out_7
  Registrador reg3 (
    .in_0(rd_0), .in_1(rd_1), .in_2(rd_2), .in_3(rd_3), .in_4(rd_4), .in_5(rd_5), .in_6(rd_6), .in_7(rd_7),
    .clk(clk), .Enable(demux_1_b3));  // open: out_0, out_1, out_2, out_3, out_4, out_5, out_6, out_7
  Registrador reg4 (
    .in_0(rd_0), .in_1(rd_1), .in_2(rd_2), .in_3(rd_3), .in_4(rd_4), .in_5(rd_5), .in_6(rd_6), .in_7(rd_7),
    .clk(clk), .Enable(demux_1_b4));  // open: out_0, out_1, out_2, out_3, out_4, out_5, out_6, out_7
  Registrador reg5 (
    .in_0(rd_0), .in_1(rd_1), .in_2(rd_2), .in_3(rd_3), .in_4(rd_4), .in_5(rd_5), .in_6(rd_6), .in_7(rd_7),
    .clk(clk), .Enable(demux_1_b5));  // open: out_0, out_1, out_2, out_3, out_4, out_5, out_6, out_7
  Registrador reg6 (
    .in_0(rd_0), .in_1(rd_1), .in_2(rd_2), .in_3(rd_3), .in_4(rd_4), .in_5(rd_5), .in_6(rd_6), .in_7(rd_7),
    .clk(clk), .Enable(demux_1_b6));  // open: out_0, out_1, out_2, out_3, out_4, out_5, out_6, out_7
  Registrador Reg7 (
    .in_0(rd_0), .in_1(rd_1), .in_2(rd_2), .in_3(rd_3), .in_4(rd_4), .in_5(rd_5), .in_6(rd_6), .in_7(rd_7),
    .clk(clk), .Enable(demux_1_b7));  // open: out_0, out_1, out_2, out_3, out_4, out_5, out_6, out_7
endmodule
